// Logisim project seq_circuit.circ as structural Verilog: 1 circuit, main circuit main
module main (
  input  in_1,
  input  in_2,
  output out_3
);

  wire clock_1_out, undriven;
  wire [7:0] adder_1_out;
  wire [7:1] undriven_2, undriven_3;

  Clock clock_1 (.out(clock_1_out));
  Adder adder_1 (.a({undriven_2, in_1}), .b({undriven_3, in_2}), .out(adder_1_out), .cin(undriven), .cout(out_3));
  D_Flip_Flop d_ff_1 (.clk(clock_1_out), .D(undriven), .Q(adder_1_out[0]));  // open: Qn, preset, en, reset
  // Pins of 1 and 8 bits meet at {undriven_3, in_2}
  // Pins of 1 and 8 bits meet at {undriven_2, in_1}
  // Pins of 1 and 8 bits meet at adder_1_out
endmodule
